// Logisim project Controller.circ as structural Verilog: 5 circuits, main circuit main
module main (
  output [7:0] outCompteur
);

  wire clock_1_out, d_ff_1_q, d_ff_2_q, d_ff_3_q, d_ff_4_q, d_ff_5_q, d_ff_6_q, d_ff_7_q, d_ff_8_q;

  Clock clock_1 (.out(clock_1_out));
  D_Flip_Flop d_ff_1 (
    .clk(clock_1_out), .D(outCompteur[0]), .Q(d_ff_1_q), .Qn(outCompteur[0]));  // open: preset, en, reset
  D_Flip_Flop d_ff_2 (
    .clk(d_ff_1_q), .D(outCompteur[1]), .Q(d_ff_2_q), .Qn(outCompteur[1]));  // open: preset, en, reset
  D_Flip_Flop d_ff_3 (
    .clk(d_ff_2_q), .D(outCompteur[2]), .Q(d_ff_3_q), .Qn(outCompteur[2]));  // open: preset, en, reset
  D_Flip_Flop d_ff_4 (
    .clk(d_ff_3_q), .D(outCompteur[3]), .Q(d_ff_4_q), .Qn(outCompteur[3]));  // open: preset, en, reset
  D_Flip_Flop d_ff_5 (
    .clk(d_ff_4_q), .D(outCompteur[4]), .Q(d_ff_5_q), .Qn(outCompteur[4]));  // open: preset, en, reset
  D_Flip_Flop d_ff_6 (
    .clk(d_ff_5_q), .D(outCompteur[5]), .Q(d_ff_6_q), .Qn(outCompteur[5]));  // open: preset, en, reset
  D_Flip_Flop d_ff_7 (
    .clk(d_ff_6_q), .D(outCompteur[6]), .Q(d_ff_7_q), .Qn(outCompteur[6]));  // open: preset, en, reset
  D_Flip_Flop d_ff_8 (
    .clk(d_ff_7_q), .D(outCompteur[7]), .Q(d_ff_8_q), .Qn(outCompteur[7]));  // open: preset, en, reset

  // Other names for the same wires on the sheet: q7 = outCompteur[0]; q6 = outCompteur[1]; q5 = outCompteur[2];
  //   q4 = outCompteur[3]; q3 = outCompteur[4]; q2 = outCompteur[5]; q1 = outCompteur[6]; q0 = outCompteur[7]
endmodule

module compteur (
  input  clocksys,
  output [7:0] outCompteur
);

  wire d_ff_1_q, d_ff_2_q, d_ff_3_q, d_ff_4_q, d_ff_5_q, d_ff_6_q, d_ff_7_q, d_ff_8_q;

  D_Flip_Flop d_ff_1 (
    .clk(clocksys), .D(outCompteur[0]), .Q(d_ff_1_q), .Qn(outCompteur[0]));  // open: preset, en, reset
  D_Flip_Flop d_ff_2 (
    .clk(d_ff_1_q), .D(outCompteur[1]), .Q(d_ff_2_q), .Qn(outCompteur[1]));  // open: preset, en, reset
  D_Flip_Flop d_ff_3 (
    .clk(d_ff_2_q), .D(outCompteur[2]), .Q(d_ff_3_q), .Qn(outCompteur[2]));  // open: preset, en, reset
  D_Flip_Flop d_ff_4 (
    .clk(d_ff_3_q), .D(outCompteur[3]), .Q(d_ff_4_q), .Qn(outCompteur[3]));  // open: preset, en, reset
  D_Flip_Flop d_ff_5 (
    .clk(d_ff_4_q), .D(outCompteur[4]), .Q(d_ff_5_q), .Qn(outCompteur[4]));  // open: preset, en, reset
  D_Flip_Flop d_ff_6 (
    .clk(d_ff_5_q), .D(outCompteur[5]), .Q(d_ff_6_q), .Qn(outCompteur[5]));  // open: preset, en, reset
  D_Flip_Flop d_ff_7 (
    .clk(d_ff_6_q), .D(outCompteur[6]), .Q(d_ff_7_q), .Qn(outCompteur[6]));  // open: preset, en, reset
  D_Flip_Flop d_ff_8 (
    .clk(d_ff_7_q), .D(outCompteur[7]), .Q(d_ff_8_q), .Qn(outCompteur[7]));  // open: preset, en, reset

  // Other names for the same wires on the sheet: q7 = outCompteur[0]; q6 = outCompteur[1]; q5 = outCompteur[2];
  //   q4 = outCompteur[3]; q3 = outCompteur[4]; q2 = outCompteur[5]; q1 = outCompteur[6]; q0 = outCompteur[7]
endmodule

// Inst
module controleur (
  input  Reset,
  output [7:0] PC,
  output Load___Store,
  output [3:0] Codop,
  output [2:0] Rm,
  output [2:0] Rd,
  output [2:0] Rn,
  output [7:0] Imm8,
  output [4:0] Imm5
);

  wire clock;
  wire [15:0] main_1_inst;

  Clock u_clock (.out(clock));
  ROM_main main_1 (.Address(PC), .Sel(clock), .Inst(main_1_inst));
  compteur Compteur (.clocksys(clock), .outCompteur(PC));
  instructionDecodeur instructiondecodeur_1 (.Inst(main_1_inst));  // open: shit, data_processing, load_store, branch
endmodule

module instructionDecodeur (
  input  [15:0] Inst,
  output shit,
  output data_processing,
  output load_store,
  output branch
);

  selecteurCategory selecteurCategory (
    .i0(Inst[10]), .i1(Inst[11]), .i2(Inst[12]), .i3(Inst[13]), .i4(Inst[14]), .i5(Inst[15]), .out0(shit),
    .out1(data_processing), .out2(load_store), .out3(branch));
endmodule

module selecteurCategory (
  input  i0,
  input  i1,
  input  i2,
  input  i3,
  input  i4,
  input  i5,
  output out0,
  output out1,
  output out2,
  output out3
);

  wire not_1_out, not_2_out, not_3_out, not_4_out, not_5_out, not_6_out, not_7_out, not_8_out, not_9_out,
       not_10_out;

  not not_1 (not_1_out, i5);
  not not_2 (not_2_out, i4);
  not not_3 (not_3_out, i5);
  not not_4 (not_4_out, i3);
  not not_5 (not_5_out, i2);
  not not_6 (not_6_out, i1);
  not not_7 (not_7_out, i0);
  not not_8 (not_8_out, i5);
  not not_9 (not_9_out, i2);
  not not_10 (not_10_out, i3);
  and and_1 (out0, not_1_out, not_2_out);
  and and_2 (out1, not_3_out, i4, not_4_out, not_5_out, not_6_out, not_7_out);
  and and_3 (out2, not_8_out, i4, i3, not_9_out);
  and and_4 (out3, i5, i4, not_10_out, i2);

  // Notes on the sheet:
  //   DATA PROCESSING
  //   LOAD STORE
  //   BRANCH
  //   SHIT ADD SUB MOVE
endmodule
