// Logisim project RAM.circ as structural Verilog: 1 circuit, main circuit main
module main (
  input  Clr,
  input  sel,
  input  ld,
  input  clk,
  input  [23:0] DataIn,
  input  [7:0] Address,
  output [23:0] out_7
);

  RAM #(.bus("separate")) ram_1 (
    .addr(Address), .din(DataIn[7:0]), .data(out_7[7:0]), .sel(sel), .clk(clk), .ld(ld), .clr(Clr));  // open: str
  RAM #(.bus("separate")) ram_2 (
    .addr(Address), .din(DataIn[15:8]), .data(out_7[15:8]), .sel(sel), .clk(clk), .ld(ld), .clr(Clr));  // open: str
  RAM #(.bus("separate")) ram_3 (
    .addr(Address), .din(DataIn[23:16]), .data(out_7[23:16]), .sel(sel), .clk(clk), .ld(ld), .clr(Clr));  // open: str

  // Other names for the same wires on the sheet: DataIn0[7:0] = DataIn[7:0]; DataIn1[7:0] = DataIn[15:8];
  //   DataIn2[7:0] = DataIn[23:16]; DataOut0[7:0] = out_7[7:0]; DataOut1[7:0] = out_7[15:8];
  //   DataOut2[7:0] = out_7[23:16]
endmodule
