// Logisim project dataProcessing.circ as structural Verilog: 1 circuit, main circuit main
module main (
  input  [15:0] in_1,
  output [3:0] opcode,
  output [2:0] rd,
  output [2:0] rn,
  output [2:0] rm
);

  wire [2:0] undriven, undriven_2;

  Multiplexer #(.select(4), .width(3)) multiplexer_1 (
    .in0(in_1[5:3]), .in1(in_1[5:3]), .in2(in_1[5:3]), .in3(in_1[5:3]), .in4(in_1[5:3]), .in5(in_1[5:3]),
    .in6(in_1[5:3]), .in7(in_1[5:3]), .in8(in_1[5:3]), .in9(undriven), .in10(in_1[5:3]), .in11(in_1[5:3]),
    .in12(in_1[5:3]), .in13(in_1[2:0]), .in14(in_1[5:3]), .in15(in_1[5:3]), .out(rm), .sel(in_1[9:6]));  // open: en
  Multiplexer #(.select(4), .width(3)) multiplexer_2 (
    .in0(in_1[2:0]), .in1(in_1[2:0]), .in2(in_1[2:0]), .in3(in_1[2:0]), .in4(in_1[2:0]), .in5(in_1[2:0]),
    .in6(in_1[2:0]), .in7(in_1[2:0]), .in8(in_1[2:0]), .in9(in_1[5:3]), .in10(in_1[2:0]), .in11(in_1[2:0]),
    .in12(in_1[2:0]), .in13(in_1[5:3]), .in14(in_1[2:0]), .in15(undriven_2), .out(rn), .sel(in_1[9:6]));  // open: en
  Multiplexer #(.select(4), .width(3)) multiplexer_3 (
    .in0(in_1[2:0]), .in1(in_1[2:0]), .in2(in_1[2:0]), .in3(in_1[2:0]), .in4(in_1[2:0]), .in5(in_1[2:0]),
    .in6(in_1[2:0]), .in7(in_1[2:0]), .in9(in_1[2:0]), .in12(in_1[2:0]), .in13(in_1[2:0]), .in14(in_1[2:0]),
    .in15(in_1[2:0]), .out(rd), .sel(in_1[9:6]));  // open: in8, in10, in11, en

  assign opcode = in_1[9:6];

  // Other names for the same wires on the sheet: part1[2:0] = in_1[2:0]; part2[2:0] = in_1[5:3]
endmodule
